# Fritzing sketch RTC_interrupt (saved by Fritzing 0.9.6b)

parts:
  Composant2 = Arduino Uno (Rev3)
  ZS-042_RTC1 = ZS-042 RTC Module

nets:
  N1: Composant2.A4/SDA, ZS-042_RTC1.SDA
  N2: Composant2.A5/SCL, ZS-042_RTC1.SCL
  N3: Composant2.D2, ZS-042_RTC1.SQW
  3V3: Composant2.3V3, ZS-042_RTC1.VCC
  GND: Composant2.GND, ZS-042_RTC1.GND
